// Logisim project AOIS_4.circ as structural Verilog
module AOIS_4_1 (
  input  A,
  input  B,
  input  C,
  output Schema_1,
  output Schema_2
);

  wire and_1_out, and_2_out, and_3_out, and_4_out, and_5_out, and_6_out, and_7_out, not_1_out, not_2_out,
       not_3_out;

  not not_1 (not_1_out, A);
  not not_2 (not_2_out, B);
  not not_3 (not_3_out, C);
  and and_1 (and_1_out, C, B);
  and and_2 (and_2_out, C, A);
  or or_1 (Schema_1, and_1_out, and_2_out, and_3_out);
  and and_3 (and_3_out, A, B);
  and and_4 (and_4_out, not_1_out, not_2_out, C);
  and and_5 (and_5_out, not_1_out, B, not_3_out);
  and and_6 (and_6_out, A, not_2_out, not_3_out);
  and and_7 (and_7_out, A, B, C);
  or or_2 (Schema_2, and_4_out, and_5_out, and_6_out, and_7_out);
endmodule

module AOIS_4_2 (
  input  x1,
  input  x2,
  input  x3,
  input  x4,
  output Schema_1,
  output Schema_2,
  output Schema_3,
  output Schema_4
);

  wire and_1_out, and_2_out, and_3_out, and_4_out, and_5_out, and_6_out, and_7_out, and_8_out, and_9_out,
       not_1_out, not_2_out, not_3_out;

  not not_1 (not_1_out, x2);
  not not_2 (not_2_out, x3);
  not not_3 (not_3_out, x4);
  and and_1 (and_1_out, not_3_out, x1);
  and and_2 (and_2_out, not_1_out, x1, not_2_out);
  and and_3 (and_3_out, not_1_out, not_3_out);
  and and_4 (and_4_out, not_1_out, not_2_out);
  and and_5 (and_5_out, not_1_out, not_2_out);
  and and_6 (and_6_out, x3, not_3_out, x2);
  and and_7 (and_7_out, not_3_out, x2);
  and and_8 (and_8_out, x3, not_3_out);
  and and_9 (and_9_out, x4, not_1_out, not_2_out);
  or or_1 (Schema_1, and_1_out, and_2_out);
  or or_2 (Schema_2, and_3_out, and_4_out);
  or or_3 (Schema_3, and_5_out, and_6_out);
  or or_4 (Schema_4, and_7_out, and_8_out, and_9_out);
endmodule
